# Fritzing sketch Raspberry Pi TA7291P (saved by Fritzing 0.9.2b)
breadboards: 1

parts:
  U1 = TA7291P [package=TA7291P]
  M1 = DC Motor
  Raspberry_Pi1 = Raspberry Pi B+
  パーツ1 = FTDI Basic Programmer
  VCC1 = Battery

nets:
  GND: U1.GND, Raspberry_Pi1.GND, パーツ1.GND, VCC1.-
  N1: U1.OUT1, M1.pin_2
  N2: U1.Vref, Raspberry_Pi1.GPIO18
  N3: U1.IN1, Raspberry_Pi1.GPIO23
  N4: U1.IN2, Raspberry_Pi1.GPIO24
  VCC: U1.Vcc, Raspberry_Pi1.5V
  N5: U1.Vs, VCC1.+
  N6: U1.OUT2, M1.pin_1
  N7: Raspberry_Pi1.GPIO15, パーツ1.TXO
  N8: Raspberry_Pi1.GPIO14, パーツ1.RXI

custom parts:
  TA7291P: The IC are Full-Bridge Driver. 4 modes available (CW / CCW / STOP / BRAKE) and PWM control. Output current:1.0 A (AVE.) 2.0 A (PEAK)
